# Fritzing sketch sensor clock (saved by Fritzing 0.8.7b)
breadboards: 1

parts:
  Part1 = Arduino Mega 2560 (Rev3)
  U1 = LCD-16X2 [package=lcd-16x2]
  DHT22 = Humidity and Temperature Sensor RHT03
  Part2 = Chronodot v2.1 DS3231
  Part3 = Barometric Pressure Sensor - BMP180 Breakout
  R1 = Resistor [tolerance=±5% resistance=10k package=THT]

nets:
  N1: Part1.A0, DHT22.Data-signal, R1.Pin_0
  N2: Part1.SCL, Part2.SCL, Part3.SCL
  N3: Part1.SDA, Part2.SDA, Part3.SDA
  VCC: Part1.3V3, DHT22.Vcc, Part3.VCC, R1.Pin_1
  5V: Part1.5V, U1.VDD, Part2.5V
  GND: Part1.GND, U1.VSS, U1.R_W, U1.K, DHT22.GND_2, Part2.GND, Part3.GND
  N4: Part1.D26, U1.RS
  N5: Part1.D30, U1.E
  N6: Part1.D34, U1.DB4
  N7: Part1.D38, U1.DB5
  N8: Part1.D42, U1.DB6
  N9: Part1.D44, U1.VO
  N10: Part1.D46, U1.A
  N11: Part1.D50, U1.DB7

custom parts:
  Chronodot v2.1 DS3231: Modified to DS3231 for naming purposes. This a custom designed module for the DS1307 Real Time Clock. The module comes fully assembled and pre-programmed with the current time (ok, so it's our current time - MST). The included Lithium coin cell battery (CR1225 41mAh) will run the module for a minimum of 9 years (17 years typical) without external 5V power. The DS1307 is accessed via the I2C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
  Barometric Pressure Sensor - BMP180 Breakout: Modified to BMP180 Description: This is a simple breakout board for the BMP085 high-precision, low-power barometric pressure sensor. The BMP085 offers a measuring range of 300 to 1100 hPa with an absolute accuracy of down to 0.03 hPa. It's based on piezo-resistive technology for EMC robustness, high accuracy and linearity as well as long term stability. This sensor supports a voltage supply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
